# Fritzing sketch Untitled Sketch 2 (saved by Fritzing 0.9.3b)

parts:
  MH-ET_LIVE_ESP32_DEVKIT1 = MH-ET LIVE ESP32 DEVKIT 38 pins
  Part1 = Current Sensor 5A
  JACK1 = 2.1mm Barrel Jack with Terminal Block  # not connected
  Mod1 = zmpt101b
  U1 = 2-Channel 5v Relay Shield [package=relay-2ch5v10a]

nets:
  N1: MH-ET_LIVE_ESP32_DEVKIT1.IO34, Mod1.OUT
  N2: MH-ET_LIVE_ESP32_DEVKIT1.IO35, Part1.OUT
  N3: MH-ET_LIVE_ESP32_DEVKIT1.IO33, U1.IN1
  N4: MH-ET_LIVE_ESP32_DEVKIT1.IO26, U1.IN2
  N5: MH-ET_LIVE_ESP32_DEVKIT1.CMD, Part1.GND
  5V: MH-ET_LIVE_ESP32_DEVKIT1.5V, Part1.VCC

notes:
  220V

custom parts:
  MH-ET LIVE ESP32 DEVKIT 38 pins: http://mh.nodebb.com/topic/2/mh-et-live-esp32-devkit
  zmpt101b: Single phase ac active output voltate transformer module.
  2-Channel 5v Relay Shield: 2 Channel 5v Relay Shield w. 2x SPD-06VDC-SD-C
